// Logisim project vending_machine_logisim.circ as structural Verilog: 1 circuit, main circuit main
module main (
  input  A,
  input  B,
  output out_3,
  output out_4
);

  wire and_1_out, and_2_out, and_3_out, and_4_out, and_5_out, and_6_out, and_7_out, and_8_out, and_9_out,
       and_10_out, C_q, clock_1_out, D_q, E_q, not_1_out, not_2_out, not_3_out, not_4_out, not_5_out,
       not_6_out, not_7_out, not_8_out, not_9_out, not_10_out, not_11_out, not_12_out, not_13_out,
       not_14_out, not_15_out, not_16_out, not_17_out, not_18_out, or_1_out, or_2_out, or_3_out, or_4_out;

  and and_1 (and_1_out, D_q, E_q);
  or or_1 (or_1_out, C_q, and_1_out);
  and and_2 (and_2_out, A, D_q);
  and and_3 (and_3_out, B, D_q, E_q);
  not not_1 (not_1_out, C_q);
  not not_2 (not_2_out, D_q);
  and and_4 (and_4_out, A, not_1_out, not_2_out);
  not not_3 (not_3_out, A);
  not not_4 (not_4_out, B);
  not not_5 (not_5_out, C_q);
  and and_5 (and_5_out, not_3_out, not_4_out, not_5_out, D_q, D_q);
  not not_6 (not_6_out, A);
  not not_7 (not_7_out, C_q);
  and and_6 (and_6_out, not_6_out, not_7_out, D_q, not_8_out);
  not not_8 (not_8_out, E_q);
  not not_9 (not_9_out, C_q);
  and and_7 (and_7_out, B, not_9_out, not_10_out, E_q);
  not not_10 (not_10_out, D_q);
  or or_2 (or_2_out, C_q, and_3_out, and_2_out);
  or or_3 (or_3_out, and_4_out, and_5_out, and_6_out, and_7_out);
  and and_8 (and_8_out, B, not_11_out, not_12_out);
  not not_11 (not_11_out, E_q);
  not not_12 (not_12_out, C_q);
  not not_13 (not_13_out, B);
  and and_9 (and_9_out, not_13_out, not_14_out, not_15_out, C_q);
  not not_14 (not_14_out, A);
  not not_15 (not_15_out, E_q);
  not not_16 (not_16_out, B);
  and and_10 (and_10_out, not_16_out, not_17_out, not_18_out, C_q);
  not not_17 (not_17_out, E_q);
  not not_18 (not_18_out, D_q);
  or or_4 (or_4_out, and_8_out, and_9_out, and_10_out);
  Clock clock_1 (.out(clock_1_out));
  D_Flip_Flop C (.clk(clock_1_out), .D(or_2_out), .Q(C_q));  // open: Qn, preset, en, reset
  D_Flip_Flop D (.clk(clock_1_out), .D(or_3_out), .Q(D_q));  // open: Qn, preset, en, reset
  D_Flip_Flop E (.clk(clock_1_out), .D(or_4_out), .Q(E_q));  // open: Qn, preset, en, reset
  D_Flip_Flop Candy (.clk(clock_1_out), .D(or_1_out), .Q(out_3));  // open: Qn, preset, en, reset
  D_Flip_Flop Change (.clk(clock_1_out), .D(C_q), .Q(out_4));  // open: Qn, preset, en, reset
endmodule
